# Fritzing sketch climatemood wiring (saved by Fritzing 0.9.10b)
circuit board: 8.46667cm x 5.64444cm
breadboards: 1

parts:
  Grove1 = Grove OLED 128x96
  RHT1 = Humidity and Temperature Sensor RHT03
  J2 = Basic Servo
  元件3 = Adafruit Feather HUZZAH ESP8266 [part_number="Adafruit #2821"]

nets:
  GND: Grove1.GND, RHT1.GND_2, J2.gnd, 元件3.GND
  VCC: Grove1.VCC, RHT1.Vcc, J2.vcc, 元件3.3.3V
  N1: Grove1.SDA, 元件3.GPIO4/SDA
  N2: Grove1.SCL, 元件3.GPIO5/SCL
  N3: RHT1.Data-signal, 元件3.GPIO2

custom parts:
  Adafruit Feather HUZZAH ESP8266: his is the Adafruit Feather HUZZAH ESP8266 - our take on an 'all-in-one' ESP8266 WiFi development board with built in USB and battery charging. Its an ESP8266 WiFi module with all the extras you need, ready to rock! We have other boards in the Feather family, check'em out here. At the Feather HUZZAH's heart is an ESP8266 WiFi microcontroller clocked at 80 MHz and at 3.3V logic. This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
